# Fritzing sketch pico (saved by Fritzing 0.9.9b)
breadboards: 1

parts:
  Pico = Raspberry Pi Pico
  R1 = Resistor [tolerance=±5% power=0.25 resistance=5.6M package=THT]
  R2 = Resistor [tolerance=±5% power=0.25 resistance=5.6M package=THT]
  Photoresistor = PHOTOCELL [package=photocell]
  R3 = Resistor [tolerance=±5% power=0.25 resistance=10k package=THT]
  Moisture = Soil Moisture Sensor
  WATER_PUMP = water pump/motor
  D1 = Rectifier Diode [part_number=1N4004 package="300 mil [THT]"]
  IRL234N = Basic FET N-Channel [package="TO220 [THT]"]
  R4 = Resistor [tolerance=±5% power=0.25 resistance=10k package=THT]

nets:
  N1: Pico.pin_12, R1.Pin_1
  N2: Pico.pin_17, R2.Pin_1
  N3: Pico.pin_18, Pico.pin_38, R3.Pin_1, Moisture.GND, IRL234N.source
  N4: Pico.pin_21, R4.Pin_0
  N5: Pico.pin_31, Moisture.SIG
  N6: Pico.pin_32, Photoresistor.P$2, R3.Pin_0
  N7: Pico.pin_36, R1.Pin_0, R2.Pin_0, Photoresistor.P$1, Moisture.VCC
  N8: Pico.pin_40, WATER_PUMP.pin_1, D1.cathode
  N9: WATER_PUMP.pin_2, D1.anode, IRL234N.drain
  N10: IRL234N.gate, R4.Pin_1

custom parts:
  Raspberry Pi Pico: Raspberry Pi Pico. Based around the RP2040 microcontroller the Pico is a low cost microcontroller device bringing Raspberry Pi quality, cost, and easy of use to the microcontroller space. Jan 2021, Split part in to two versions: tht (this one) and SMD. This one will drill holes for a .1 in header in pcb to allow plugging in the module as well as providing pads to solder the module to the top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
  water pump/motor: WATER PUMP BY ARDUBLOCKTR
